# Fritzing sketch iot200-siemens-improved (saved by Fritzing 0.9.3b)
circuit board: 7.33412cm x 5.73052cm
breadboards: 1

parts:
  R3 = Resistor [tolerance=±5% resistance=4.7k package=THT]
  R4 = Resistor [tolerance=±5% resistance=4.7k package=THT]
  ALIM_I2C = female pin header, 3 pins [form="♀ (female)"]
  Keyboard = Header 3 [package=jst-3-pth]
  I2C_1 = Grove 4 Digit Display
  J2 = female pin header, 6 pins [form="♀ (female)"]
  J3 = female pin header, 8 pins [form="♀ (female)"]
  J4 = female pin header, 2 pins [form="♀ (female)"]
  Part1 = Arduino Uno (Rev3) [part_number=NO_USE]  # not connected
  DC/DC_CONVERTER = TracoPower TSR-1 DC/DC Converter [part_number="TSR 2-2450"]
  EXT_V+ = screw terminal, 2 pins
  U2 = Molex RJ45 Jack [part_number="BUS I2C" package=rj45-8]
  IC1 = FDC6327C [package="Super SOT"]
  C1 = Ceramic Capacitor [capacitance=0.1nF part_number=100V package="100 mil [THT, multilayer]"]
  C2 = Ceramic Capacitor [capacitance=1nF voltage=16V package="100 mil [THT, multilayer]"]
  R7 = Resistor [tolerance=±5% resistance=1M package=THT]
  R8 = Resistor [tolerance=±5% resistance=1.2M package=THT]
  D2 = Zener Diode [part_number=SMAJ18A breakdown_voltage=3.6V package="300 mil [THT]"]
  IC2 = FDC6327C [package="Super SOT"]
  C3 = Ceramic Capacitor [capacitance=0.1nF part_number=100V package="100 mil [THT, multilayer]"]
  C4 = Ceramic Capacitor [capacitance=1nF voltage=16V package="100 mil [THT, multilayer]"]
  R9 = Resistor [tolerance=±5% resistance=1M package=THT]
  D3 = Zener Diode [part_number=SMAJ18A breakdown_voltage=3.6V package="300 mil [THT]"]
  R10 = Resistor [tolerance=±5% resistance=1.2M package=THT]
  J6 = female pin header, 2 pins [form="♀ (female)"]
  I2C_2 = Grove 4 Digit Display
  I2C_3 = Grove 4 Digit Display
  RELAY = Grove 4 Digit Display
  BUTTON = Grove 4 Digit Display
  UART = Grove 4 Digit Display
  J1 = female pin header, 4 pins [form="♀ (female)"]

nets:
  I2C SCL: R3.Pin_0, I2C_1.CLK, J4.pin1, U2.6, I2C_2.CLK, I2C_3.CLK
  I2C VCC: R3.Pin_1, R4.Pin_1, I2C_1.VCC, U2.5, IC1.4, C1.1, D2.cathode, I2C_2.VCC, I2C_3.VCC
  I2C SDA: R4.Pin_0, I2C_1.DIO, J4.pin2, U2.4, I2C_2.DIO, I2C_3.DIO
  MCU_5V: ALIM_I2C.pin1, Keyboard.1, RELAY.VCC, BUTTON.VCC, UART.VCC, J1.pin1
  N1: ALIM_I2C.pin2, IC1.2, C2.1, R7.Pin_1
  N2: ALIM_I2C.pin3, DC/DC_CONVERTER.3
  A5: Keyboard.2, J2.pin6
  GND: Keyboard.3, I2C_1.GND, DC/DC_CONVERTER.2, EXT_V+.pin2, U2.7, IC1.5, C1.0, D2.anode, IC2.5, C3.0, D3.anode, I2C_2.GND, I2C_3.GND, RELAY.GND, BUTTON.GND, UART.GND, J1.pin2, J1.pin3
  UART_RX: J3.pin1, UART.CLK
  UART_TX: J3.pin2, UART.DIO
  IO2: J3.pin3, U2.3
  IO3: J3.pin4, U2.1
  24V_CTRL: J3.pin5, IC2.1
  I2C_BUS_CTRL: J3.pin6, IC1.1
  IO7: J3.pin8, BUTTON.CLK
  VIN: DC/DC_CONVERTER.1, IC2.2, C4.1, R9.Pin_1, J1.pin4
  N3: EXT_V+.pin1, IC2.4, C3.1, D3.cathode
  N4: IC1.3, C2.0, R7.Pin_0, R8.Pin_0
  N5: IC1.6, R8.Pin_1
  N6: IC2.3, C4.0, R9.Pin_0, R10.Pin_0
  N7: IC2.6, R10.Pin_1
  IO8: J6.pin1, RELAY.CLK

notes:
  5V JMP
  I2C BUS pull-ups
  SCL
  SDA
  D8
  5V
  GND
  A5
  24V D4
  D3
  D2
  HEADERS MCU
  EXT SWITCHABLE V+
  I2C SWITCHABLE VCC
  I2C BUS D5
  Air Liquide / Joshfire, SIEMENS SIMATICIOT 2040 BOARD, 1.0
  VOUT
  RJ45 I2C BUS
  Only for pin reference
  D7
  I2C BUS
  GPIOS
  MCU
  VCC / VIN SWITCHS
  Air Liquide / Joshfire
  5V_MCU
  5V_VIN_DC

custom parts:
  TracoPower TSR-1 DC/DC Converter: TracoPower TSR 1-2450 DC Converter Input6.5 - 36VDC Max current 1A
  Molex RJ45 Jack: RJ45 Jack Molex 446200001
  FDC6327C: Dual N & P-Channel 2.5V Specified PowerTrenchTM MOSFET These N & P-Channel 2.5V specified MOSFETs are produced using Fairchild Semiconductor's advanced PowerTrench process that has been especially tailored to minimize on-state resistance and yet maintain low gate charge for superior switching performance.
