# Fritzing sketch iot200-siemens-new-mosfets (saved by Fritzing 0.9.3b)
circuit board: 7.33412cm x 5.73052cm
breadboards: 1

parts:
  R3 = Resistor [tolerance=±5% resistance=4.7k package=THT]
  R4 = Resistor [tolerance=±5% resistance=4.7k package=THT]
  ORIG_5V = female pin header, 3 pins [form="♀ (female)"]
  Keyboard = Header 3 [package=jst-3-pth]
  Screen = Grove 4 Digit Display
  J1 = female pin header, 8 pins [form="♀ (female)"]
  J2 = female pin header, 6 pins [form="♀ (female)"]
  J3 = female pin header, 8 pins [form="♀ (female)"]
  J4 = female pin header, 2 pins [form="♀ (female)"]
  J5 = female pin header, 2 pins [form="♀ (female)"]
  Part1 = Arduino Uno (Rev3) [part_number=NO_USE]  # not connected
  DC/DC_CONVERTER = TracoPower TSR-1 DC/DC Converter [part_number="TSR 2-2450"]
  EXT_V+ = screw terminal, 2 pins
  U2 = Molex RJ45 Jack [part_number="BUS I2C" package=rj45-8]
  IC1 = FDC6327C [package="Super SOT"]
  C1 = Ceramic Capacitor [capacitance=0.1nF part_number=100V package="100 mil [THT, multilayer]"]
  C2 = Ceramic Capacitor [capacitance=1nF voltage=16V package="100 mil [THT, multilayer]"]
  R7 = Resistor [tolerance=±5% resistance=1M package=THT]
  R8 = Resistor [tolerance=±5% resistance=1.2M package=THT]
  D2 = Zener Diode [part_number=SMAJ18A breakdown_voltage=3.6V package="300 mil [THT]"]
  IC2 = FDC6327C [package="Super SOT"]
  C3 = Ceramic Capacitor [capacitance=0.1nF part_number=100V package="100 mil [THT, multilayer]"]
  C4 = Ceramic Capacitor [capacitance=1nF voltage=16V package="100 mil [THT, multilayer]"]
  R9 = Resistor [tolerance=±5% resistance=1M package=THT]
  D3 = Zener Diode [part_number=SMAJ18A breakdown_voltage=3.6V package="300 mil [THT]"]
  R10 = Resistor [tolerance=±5% resistance=1.2M package=THT]

nets:
  I2C SCL: R3.Pin_0, Screen.CLK, J4.pin1, U2.6
  5V: R3.Pin_1, R4.Pin_1, Screen.VCC, U2.5, IC1.4, C1.1, D2.cathode
  I2C SDA: R4.Pin_0, Screen.DIO, J4.pin2, U2.4
  N1: ORIG_5V.pin1, Keyboard.1, J1.pin5
  N2: ORIG_5V.pin2, IC1.2, C2.1, R7.Pin_1
  N3: ORIG_5V.pin3, DC/DC_CONVERTER.3
  N4: Keyboard.2, J2.pin6
  GND: Keyboard.3, Screen.GND, J1.pin6, J1.pin7, DC/DC_CONVERTER.2, EXT_V+.pin2, U2.7, IC1.5, C1.0, D2.anode, IC2.5, C3.0, D3.anode
  VIN: J1.pin8, DC/DC_CONVERTER.1, IC2.2, C4.1, R9.Pin_1
  IO2: J3.pin3, U2.3
  PIN IO3: J3.pin4, U2.1
  24V_CTRL: J3.pin5, IC2.1
  BUS_CTRL: J3.pin6, IC1.1
  IO13: J5.pin2, U2.8
  N5: EXT_V+.pin1, IC2.4, C3.1, D3.cathode
  N6: IC1.3, C2.0, R7.Pin_0, R8.Pin_0
  N7: IC1.6, R8.Pin_1
  N8: IC2.3, C4.0, R9.Pin_0, R10.Pin_0
  N9: IC2.6, R10.Pin_1

notes:
  5V
  I2C Bus pull-ups
  SCL
  SDA
  13
  GND
  A5
  24V D4
  D3
  D2
  HEADERS MCU
  EXT SWITCHABLE V+
  I2C SWITCHABLE V+
  I2C BUS D5
  Air Liquide / Joshfire, SIEMENS SIMATICIOT 2040 BOARD, 1.0
  VOUT
  RJ45 I2C BUS
  Only for pin reference

custom parts:
  TracoPower TSR-1 DC/DC Converter: TracoPower TSR 1-2450 DC Converter Input6.5 - 36VDC Max current 1A
  Molex RJ45 Jack: RJ45 Jack Molex 446200001
  FDC6327C: Dual N & P-Channel 2.5V Specified PowerTrenchTM MOSFET These N & P-Channel 2.5V specified MOSFETs are produced using Fairchild Semiconductor's advanced PowerTrench process that has been especially tailored to minimize on-state resistance and yet maintain low gate charge for superior switching performance.
