# Fritzing sketch iot200-siemens (saved by Fritzing 0.9.3b)
circuit board: 7.33412cm x 5.73052cm
breadboards: 1

parts:
  R3 = Resistor [tolerance=±5% resistance=4.7k package=THT]
  R4 = Resistor [tolerance=±5% resistance=4.7k package=THT]
  R1 = Resistor [tolerance=±5% resistance=220 package=THT]
  ORIG_5V = female pin header, 3 pins [form="♀ (female)"]
  U1 = RJ45 Jack [part_number="BUS I2C" package=rj45-8]
  Keyboard = Header 3 [package=jst-3-pth]
  Screen = Grove 4 Digit Display
  J1 = female pin header, 8 pins [form="♀ (female)"]
  J2 = female pin header, 6 pins [form="♀ (female)"]
  J3 = female pin header, 8 pins [form="♀ (female)"]
  J4 = female pin header, 2 pins [form="♀ (female)"]
  J5 = female pin header, 2 pins [form="♀ (female)"]
  Part1 = Arduino Uno (Rev3) [part_number=NO_USE]  # not connected
  DC/DC_CONVERTER = TracoPower TSR-1 DC/DC Converter [part_number="TSR 2-2450"]
  TIP120 = npn-Powertransistor [part_number=TIP120 package="TO220 [THT]"]
  Pad1 = Pad [width=9.3133427407407403 height=10.141185185185181 connect=center]  # not connected
  MOSFET = Basic FET N-Channel [part_number=MOSFET package="TO220 [THT]"]
  R5 = Resistor [tolerance=±5% resistance=220 package=THT]
  R6 = Resistor [tolerance=±5% resistance=100k package=THT]
  D1 = Rectifier Diode [part_number=1N4001 package="300 mil [THT]"]
  Pad2 = Pad [width=9.3133427407407403 height=10.141185185185181 connect=center]  # not connected
  EXT_V+ = screw terminal, 2 pins

nets:
  I2C SCL: R3.Pin_0, U1.6, Screen.CLK, J4.pin1
  5V: R3.Pin_1, R4.Pin_1, ORIG_5V.pin2, U1.5, Screen.VCC
  I2C SDA: R4.Pin_0, U1.4, Screen.DIO, J4.pin2
  N1: R1.Pin_0, J3.pin8
  N2: R1.Pin_1, TIP120.base
  N3: ORIG_5V.pin1, Keyboard.1, J1.pin5
  N4: ORIG_5V.pin3, DC/DC_CONVERTER.3
  N5: U1.1, J3.pin4
  N6: U1.2, J3.pin5
  N7: U1.3, J3.pin3
  GND: U1.7, Keyboard.3, Screen.GND, J1.pin6, J1.pin7, DC/DC_CONVERTER.2, TIP120.collector, TIP120.emitter, MOSFET.source, R6.Pin_0
  N8: U1.8, J5.pin2
  N9: Keyboard.2, J2.pin6
  VIN: J1.pin8, DC/DC_CONVERTER.1, D1.cathode, EXT_V+.pin1
  N10: J3.pin7, R5.Pin_0
  N11: MOSFET.gate, R5.Pin_1, R6.Pin_1
  N12: MOSFET.drain, D1.anode, EXT_V+.pin2

notes:
  5V
  I2C Bus pull-ups
  SCL
  SDA
  13
  GND
  A5
  D4
  D3
  D2
  TIP120 D7
  HEADERS MCU
  EXT SWITCHABLE V+
  I2C SWITCHABLE V+
  MOSFET D6
  Air Liquide / Joshfire, SIEMENS SIMATICIOT 2040 BOARD, 1.0
  For pin reference only
  VOUT

custom parts:
  TracoPower TSR-1 DC/DC Converter: TracoPower TSR 1-2450 DC Converter Input6.5 - 36VDC Max current 1A
