# Fritzing sketch iot200-siemens-30V_vBufferTCA9517_vVertical_CMSDIODE (saved by Fritzing 0.9.3b)
circuit board: 7.3694cm x 5.73052cm
breadboards: 1

parts:
  R3 = Resistor [tolerance=±5% resistance=4.7k package=THT]
  R4 = Resistor [tolerance=±5% resistance=4.7k package=THT]
  ALIM_I2C = female pin header, 3 pins [form="♀ (female)"]
  J2 = Header 3 [package=jst-3-pth]
  J101 = Grove 4 Digit Display
  J3 = female pin header, 8 pins [form="♀ (female)"]
  J4 = female pin header, 2 pins [form="♀ (female)"]
  Part1 = Arduino Uno (Rev3) [part_number=NO_USE]  # not connected
  IC3 = TracoPower TSR-1 DC/DC Converter [part_number="TSR 2-2450"]
  C1 = Ceramic Capacitor [capacitance=0.1nF part_number=100V package="100 mil [THT, multilayer]"]
  C2 = Ceramic Capacitor [capacitance=1nF voltage=16V package="100 mil [THT, multilayer]"]
  R7 = Resistor [tolerance=±5% resistance=1M package=THT]
  R8 = Resistor [tolerance=±5% resistance=470k package=THT]
  C3 = Ceramic Capacitor [capacitance=0.1nF part_number=100V package="100 mil [THT, multilayer]"]
  C4 = Ceramic Capacitor [capacitance=1nF voltage=16V package="100 mil [THT, multilayer]"]
  R9 = Resistor [tolerance=±5% resistance=1M package=THT]
  R10 = Resistor [tolerance=±5% resistance=470k package=THT]
  J6 = female pin header, 2 pins [form="♀ (female)"]
  J102 = Grove 4 Digit Display
  J103 = Grove 4 Digit Display
  J105 = Grove 4 Digit Display
  J104 = Grove 4 Digit Display
  J106 = Grove 4 Digit Display
  J1 = female pin header, 4 pins [form="♀ (female)"]
  IC1 = SO08 [chip_label=FDS8958A package=SO]
  IC2 = SO08 [chip_label=FDS8958A package=SO]
  J2_2 = female pin header, 6 pins [form="♀ (female)"]
  R11 = Resistor [tolerance=±5% resistance=4.7k package=THT]
  R12 = Resistor [tolerance=±5% resistance=4.7k package=THT]
  C5 = Ceramic Capacitor [capacitance=10nF part_number=100V package="100 mil [THT, multilayer]"]
  IC5 = SO08 [chip_label=TCA9517 package=SO]
  U3 = RJ45 Jack [package=rj45-8]
  J1_2 = screw terminal, 2 pins
  D2 = Zener Diode [part_number=1N4732A breakdown_voltage=3.6V package="Melf DO-213 AB [SMD]"]
  D3 = Zener Diode [part_number=1N4732A breakdown_voltage=3.6V package="Melf DO-213 AB [SMD]"]

nets:
  I2C SCL IOT: R3.Pin_0, J4.pin1, IC5.7
  5V: R3.Pin_1, R4.Pin_1, ALIM_I2C.pin2, C2.1, R7.Pin_1, IC1.3, R11.Pin_1, R12.Pin_1, C5.0, IC5.1, IC5.8
  I2C SDA IOT: R4.Pin_0, J4.pin2, IC5.6
  MCU_5V: ALIM_I2C.pin1, J2.1, J105.VCC, J104.VCC, J106.VCC, J1.pin1
  N1: ALIM_I2C.pin3, IC3.3
  A0: J2.2, J2_2.pin1
  GND: J2.3, J101.GND, IC3.2, C1.0, C3.0, J102.GND, J103.GND, J105.GND, J104.GND, J106.GND, J1.pin2, J1.pin3, IC1.1, IC2.1, C5.1, IC5.4, U3.7, J1_2.pin2, D2.anode, D3.anode
  I2C VCC: J101.VCC, C1.1, J102.VCC, J103.VCC, IC1.5, U3.5, D2.cathode
  I2C SDA OUT: J101.DIO, J102.DIO, J103.DIO, R11.Pin_0, IC5.3, U3.4
  I2C SCL OUT: J101.CLK, J102.CLK, J103.CLK, R12.Pin_0, IC5.2, U3.6
  UART_RX: J3.pin1, J106.CLK
  UART_TX: J3.pin2, J106.DIO
  IO2: J3.pin3, U3.3
  IO3: J3.pin4, U3.1
  I2C_BUS_CTRL: J3.pin5, IC1.2, IC5.5
  IO7: J3.pin8, J104.CLK
  VIN: IC3.1, C4.1, R9.Pin_1, J1.pin4, IC2.3
  N2: C2.0, R7.Pin_0, R8.Pin_0, IC1.4
  N3: R8.Pin_1, IC1.8
  N4: C3.1, IC2.5, J1_2.pin1, D3.cathode
  N5: C4.0, R9.Pin_0, R10.Pin_0, IC2.4
  N6: R10.Pin_1, IC2.8
  IO8: J6.pin1, J105.CLK
  24V_CTRL: IC2.2, J2_2.pin2

notes:
  5V JMP
  I2C BUS pull-ups
  CL
  DA
  D8
  5V
  GND
  A0
  I2C BUS D4
  D3
  D2
  HEADERS MCU
  EXT SWITCHABLE V+
  I2C SWITCHABLE VCC
  Air Liquide / Joshfire, SIEMENS SIMATICIOT 2040 BOARD, 2
  RJ45 I2C BUS
  Only for pin reference
  D7
  I2C BUS
  GPIOS
  MCU
  VCC / VIN SWITCHS
  Air Liquide / Joshfire
  5V_MCU
  5V_VIN
  BUTTON
  RELAY
  I2C 1, 2 & 3
  UART
  U1
  A1 24V

custom parts:
  TracoPower TSR-1 DC/DC Converter: TracoPower TSR 1-2450 DC Converter Input6.5 - 36VDC Max current 1A
